# Fritzing sketch Control_ledRGB (saved by Fritzing 0.9.3b)
breadboards: 1

parts:
  LED1 = RGB LED (com. anode, rbg) [package="5 mm [THT]"]
  R1 = Resistor [tolerance=±5% resistance=220 package=THT]
  R2 = Resistor [tolerance=±5% resistance=220 package=THT]
  Componente1 = Arduino Uno (Rev3)
  IR1 = TSOP312.., 314.. [package=THT]
  R3 = Resistor [tolerance=±5% resistance=220 package="1206 [SMD]"]

nets:
  N1: LED1.red_cathode, R1.Pin_1
  GND: LED1.common_anode, Componente1.GND, IR1.GND
  N2: LED1.blue_cathode, R2.Pin_1
  N3: LED1.green_cathode, R3.Pin_1
  N4: R1.Pin_0, Componente1.D6_PWM
  N5: R2.Pin_0, Componente1.D5_PWM
  N6: Componente1.D11_PWM/MOSI, IR1.Data
  N7: Componente1.D3_PWM, R3.Pin_0
  N8: Componente1.5V, IR1.Vs
